// Logisim project vertebrate.circ as structural Verilog: 21 circuits, main circuit Simulation
module CPU (
  input  [15:0] din,
  input  clk,
  output MEMLD,
  output [11:0] Addrout,
  output [15:0] Dout,
  output [15:0] R0
);

  wire ARMUX, IRLD, MUX, PCINC, PCLD, REGLD, Z, ZF, ZFLD;
  wire [2:0] dr, opc, sr1, sr2;
  wire [3:0] ALUC;
  wire [11:0] instr, instr_in, jmp, PC;
  wire [15:0] multiplexer_1_out, out, R1;

  Data_Receiver Data_Receiver (.din(din), .instr(instr_in), .opc(opc));
  ALU alu_1 (.op1(R1), .op2(Dout), .s(ALUC), .out(out), .Z(Z));
  Data_Transmitter Data_Transmitter (.pc(PC), .R1(R1), .s(ARMUX), .addr(Addrout));
  Instruction_Decoder Instruction_Decoder (.instr(instr), .dr(dr), .sr1(sr1), .sr2(sr2), .jmp(jmp), .ALUC(ALUC));
  IR ir_1 (.ld(instr_in), .en(IRLD), .clk(clk), .rd(instr));
  Multiplexer #(.width(16), .enable("false")) multiplexer_1 (.in0(out), .in1(din), .out(multiplexer_1_out), .sel(MUX));
  Control_Unit_Microprogrammed Control_Unit (
    .z(ZF), .opc(opc), .clk(clk), .PCINC(PCINC), .MUX(MUX), .ARMUX(ARMUX), .IRLD(IRLD), .PCLD(PCLD),
    .REGLD(REGLD), .ZFLD(ZFLD), .MEMLD(MEMLD));
  PC pc_1 (.ld(jmp), .inc(PCINC), .jmp(PCLD), .clk(clk), .rd(PC));
  Register_File register_file_1 (
    .sw(dr), .en(REGLD), .ld(multiplexer_1_out), .clk(clk), .sr1(sr1), .sr2(sr2), .R0(R0), .R1(R1), .R2(Dout));
  ZF zf_1 (.ld(Z), .en(ZFLD), .clk(clk), .rd(ZF));

  // Other names for the same wires on the sheet: R2[15:0] = Dout

  // Notes on the sheet:
  //   Input
  //   Output
  //   These are trivial circuits created for reducing the complexity in the CPU
endmodule

module ALU_1 (
  input  op1,
  input  op2,
  input  cin,
  input  [2:0] s,
  output cout,
  output out
);

  wire and_1_out, and_2_out, and_3_out, not_1_out, or_1_out, xor_1_out, xor_2_out, xor_3_out;

  xor xor_1 (xor_1_out, op1, op2);
  and and_1 (and_1_out, xor_1_out, cin);
  and and_2 (and_2_out, op2, op1);
  and and_3 (and_3_out, op1, op2);
  or or_1 (or_1_out, op1, op2);
  not not_1 (not_1_out, op1);
  xor xor_2 (xor_2_out, xor_1_out, cin);
  xor xor_3 (xor_3_out, op1, op2);
  or or_2 (cout, and_1_out, and_2_out);
  Multiplexer #(.select(3), .enable("false")) multiplexer_1 (
    .in0(xor_2_out), .in1(and_3_out), .in2(or_1_out), .in3(xor_3_out), .in4(not_1_out), .in5(op1), .out(out),
    .sel(s));  // open: in6, in7
endmodule

module ALU (
  input  [15:0] op1,
  input  [15:0] op2,
  input  [3:0] s,
  output [15:0] out,
  output Z
);

  wire alu_1_1_cout, alu_1_2_cout, alu_1_3_cout, alu_1_4_cout, alu_1_5_cout, alu_1_6_cout, alu_1_7_cout,
       alu_1_8_cout, alu_1_9_cout, alu_1_10_cout, alu_1_11_cout, alu_1_12_cout, alu_1_13_cout, alu_1_14_cout,
       alu_1_15_cout, and_1_out, and_2_out, and_3_out, and_4_out, and_5_out, and_6_out, and_7_out, and_8_out,
       and_9_out, and_10_out, not_1_out, not_2_out, not_3_out, not_4_out, not_5_out, not_6_out, not_7_out,
       not_8_out, not_9_out, not_10_out, not_11_out, not_12_out, not_13_out;
  wire [1:0] or_5_out;
  wire [2:0] or_1_out;
  wire [15:0] multiplexer_1_out, not_14_out;

  not not_1 (not_1_out, s[0]);
  not not_2 (not_2_out, s[1]);
  not not_3 (not_3_out, s[0]);
  not not_4 (not_4_out, s[3]);
  not not_5 (not_5_out, s[3]);
  not not_6 (not_6_out, s[1]);
  not not_7 (not_7_out, s[2]);
  not not_8 (not_8_out, s[0]);
  not not_9 (not_9_out, s[2]);
  not not_10 (not_10_out, s[1]);
  not not_11 (not_11_out, s[2]);
  not not_12 (not_12_out, s[3]);
  not not_13 (not_13_out, s[2]);
  and and_1 (and_1_out, ~s[3], ~s[2], ~s[1], s[0]);  // AND_Gate
  and and_2 (and_2_out, not_1_out, not_2_out, s[3]);
  and and_3 (and_3_out, not_3_out, s[1], not_4_out);
  and and_4 (and_4_out, s[0], s[1], not_5_out);
  and and_5 (and_5_out, not_6_out, s[3]);
  and and_6 (and_6_out, s[0], s[2]);
  and and_7 (and_7_out, s[3], s[1], not_7_out, not_8_out);
  and and_8 (and_8_out, s[3], s[1], s[0], not_9_out);
  and and_9 (and_9_out, s[0], not_10_out, not_11_out, not_12_out);
  and and_10 (and_10_out, s[0], s[1], s[3], not_13_out);
  or or_1 (or_1_out[0], and_2_out, s[2], and_3_out);
  or or_2 (or_1_out[1], s[2], and_4_out);
  or or_3 (or_1_out[2], and_5_out, and_6_out);
  or or_4 (or_5_out[1], and_7_out, and_8_out);
  or or_5 (or_5_out[0], and_9_out, and_10_out);
  assign not_14_out = ~op2;  // NOT_Gate not_14, 16 bits wide
  Multiplexer #(.select(2), .width(16), .enable("false")) multiplexer_1 (
    .in0(op2), .in1(not_14_out), .in2(16'h1), .in3({16{1'b1}}), .out(multiplexer_1_out), .sel(or_5_out));
  ALU_1 alu_1_1 (
    .op1(op1[0]), .op2(multiplexer_1_out[0]), .cin(and_1_out), .cout(alu_1_1_cout), .out(out[0]), .s(or_1_out));
  ALU_1 alu_1_2 (
    .op1(op1[1]), .op2(multiplexer_1_out[1]), .cin(alu_1_1_cout), .cout(alu_1_2_cout), .out(out[1]),
    .s(or_1_out));
  ALU_1 alu_1_3 (
    .op1(op1[2]), .op2(multiplexer_1_out[2]), .cin(alu_1_2_cout), .cout(alu_1_3_cout), .out(out[2]),
    .s(or_1_out));
  ALU_1 alu_1_4 (
    .op1(op1[3]), .op2(multiplexer_1_out[3]), .cin(alu_1_3_cout), .cout(alu_1_4_cout), .out(out[3]),
    .s(or_1_out));
  ALU_1 alu_1_5 (
    .op1(op1[4]), .op2(multiplexer_1_out[4]), .cin(alu_1_4_cout), .cout(alu_1_5_cout), .out(out[4]),
    .s(or_1_out));
  ALU_1 alu_1_6 (
    .op1(op1[5]), .op2(multiplexer_1_out[5]), .cin(alu_1_5_cout), .cout(alu_1_6_cout), .out(out[5]),
    .s(or_1_out));
  ALU_1 alu_1_7 (
    .op1(op1[6]), .op2(multiplexer_1_out[6]), .cin(alu_1_6_cout), .cout(alu_1_7_cout), .out(out[6]),
    .s(or_1_out));
  ALU_1 alu_1_8 (
    .op1(op1[7]), .op2(multiplexer_1_out[7]), .cin(alu_1_7_cout), .cout(alu_1_8_cout), .out(out[7]),
    .s(or_1_out));
  ALU_1 alu_1_9 (
    .op1(op1[8]), .op2(multiplexer_1_out[8]), .cin(alu_1_8_cout), .cout(alu_1_9_cout), .out(out[8]),
    .s(or_1_out));
  ALU_1 alu_1_10 (
    .op1(op1[9]), .op2(multiplexer_1_out[9]), .cin(alu_1_9_cout), .cout(alu_1_10_cout), .out(out[9]),
    .s(or_1_out));
  ALU_1 alu_1_11 (
    .op1(op1[10]), .op2(multiplexer_1_out[10]), .cin(alu_1_10_cout), .cout(alu_1_11_cout), .out(out[10]),
    .s(or_1_out));
  ALU_1 alu_1_12 (
    .op1(op1[11]), .op2(multiplexer_1_out[11]), .cin(alu_1_11_cout), .cout(alu_1_12_cout), .out(out[11]),
    .s(or_1_out));
  ALU_1 alu_1_13 (
    .op1(op1[12]), .op2(multiplexer_1_out[12]), .cin(alu_1_12_cout), .cout(alu_1_13_cout), .out(out[12]),
    .s(or_1_out));
  ALU_1 alu_1_14 (
    .op1(op1[13]), .op2(multiplexer_1_out[13]), .cin(alu_1_13_cout), .cout(alu_1_14_cout), .out(out[13]),
    .s(or_1_out));
  ALU_1 alu_1_15 (
    .op1(op1[14]), .op2(multiplexer_1_out[14]), .cin(alu_1_14_cout), .cout(alu_1_15_cout), .out(out[14]),
    .s(or_1_out));
  ALU_1 alu_1_16 (
    .op1(op1[15]), .op2(multiplexer_1_out[15]), .cin(alu_1_15_cout), .out(out[15]), .s(or_1_out));  // open: cout
  Comparator #(.width(16), .mode("unsigned")) comparator_1 (.a(out), .b({16{1'b0}}), .eq(Z));  // open: gt, lt
endmodule

module PC (
  input  [11:0] ld,
  input  inc,
  input  jmp,
  input  clk,
  output [11:0] rd
);

  wire or_1_out;
  wire [11:0] adder_1_out, multiplexer_1_out;

  Multiplexer #(.width(12), .enable("false")) multiplexer_1 (.in0(ld), .in1(12'h1), .out(multiplexer_1_out), .sel(inc));
  Register_12 register_12_1 (.ld(adder_1_out), .en(or_1_out), .clk(clk), .rd(rd));
  or or_1 (or_1_out, inc, jmp);
  Adder #(.width(12)) adder_1 (.a(multiplexer_1_out), .b(rd), .out(adder_1_out));  // open: cin, cout
endmodule

module Control_Unit_Hardwired (
  input  [2:0] opc,
  input  z,
  input  clk,
  output PCINC,
  output MUX,
  output ARMUX,
  output IRLD,
  output PCLD,
  output REGLD,
  output ZFLD,
  output MEMLD
);

  wire [2:0] State_Manager_state;

  State_Manager State_Manager (.opc(opc), .z(z), .clk(clk), .state(State_Manager_state));
  Signal_Generator Signal_Generator (
    .state(State_Manager_state), .PCINC(PCINC), .IRLD(IRLD), .ARMUX(ARMUX), .MUX(MUX), .PCLD(PCLD),
    .REGLD(REGLD), .ZFLD(ZFLD), .MEMLD(MEMLD));

  // Notes on the sheet:
  //   Although the microprogrammed control unit is used in the CPU, we did not want to remove our work from the project
endmodule

module Register_File (
  input  [2:0] sw,
  input  en,
  input  [15:0] ld,
  input  clk,
  input  [2:0] sr1,
  input  [2:0] sr2,
  output [15:0] R0,
  output [15:0] R1,
  output [15:0] R2
);

  wire and_1_out, and_2_out, and_3_out, and_4_out, and_5_out, and_6_out, and_7_out, and_8_out,
       decoder_1_out0, decoder_1_out1, decoder_1_out2, decoder_1_out3, decoder_1_out4, decoder_1_out5,
       decoder_1_out6, decoder_1_out7;
  wire [15:0] register_16_1_rd, register_16_2_rd, register_16_3_rd, register_16_4_rd, register_16_5_rd,
       register_16_6_rd, register_16_7_rd;

  and and_1 (and_1_out, en, decoder_1_out7);
  Register_16 register_16_1 (.ld(ld), .en(and_1_out), .clk(clk), .rd(register_16_1_rd));
  and and_2 (and_2_out, en, decoder_1_out6);
  Register_16 register_16_2 (.ld(ld), .en(and_2_out), .clk(clk), .rd(register_16_2_rd));
  Multiplexer #(.select(3), .width(16), .enable("false")) multiplexer_1 (
    .in0(R0), .in1(register_16_7_rd), .in2(register_16_6_rd), .in3(register_16_5_rd), .in4(register_16_4_rd),
    .in5(register_16_3_rd), .in6(register_16_2_rd), .in7(register_16_1_rd), .out(R1), .sel(sr1));
  and and_3 (and_3_out, en, decoder_1_out5);
  Register_16 register_16_3 (.ld(ld), .en(and_3_out), .clk(clk), .rd(register_16_3_rd));
  Decoder #(.select(3), .enable("false")) decoder_1 (
    .out0(decoder_1_out0), .out1(decoder_1_out1), .out2(decoder_1_out2), .out3(decoder_1_out3),
    .out4(decoder_1_out4), .out5(decoder_1_out5), .out6(decoder_1_out6), .out7(decoder_1_out7), .sel(sw));
  and and_4 (and_4_out, en, decoder_1_out4);
  Register_16 register_16_4 (.ld(ld), .en(and_4_out), .clk(clk), .rd(register_16_4_rd));
  and and_5 (and_5_out, decoder_1_out3, en);
  Register_16 register_16_5 (.ld(ld), .en(and_5_out), .clk(clk), .rd(register_16_5_rd));
  and and_6 (and_6_out, decoder_1_out1, en);
  and and_7 (and_7_out, decoder_1_out2, en);
  Register_16 register_16_6 (.ld(ld), .en(and_7_out), .clk(clk), .rd(register_16_6_rd));
  and and_8 (and_8_out, decoder_1_out0, en);
  Register_16 register_16_7 (.ld(ld), .en(and_6_out), .clk(clk), .rd(register_16_7_rd));
  Register_16 register_16_8 (.ld(ld), .en(and_8_out), .clk(clk), .rd(R0));
  Multiplexer #(.select(3), .width(16), .enable("false")) multiplexer_2 (
    .in0(R0), .in1(register_16_7_rd), .in2(register_16_6_rd), .in3(register_16_5_rd), .in4(register_16_4_rd),
    .in5(register_16_3_rd), .in6(register_16_2_rd), .in7(register_16_1_rd), .out(R2), .sel(sr2));
endmodule

module Register_12 (
  input  [11:0] ld,
  input  en,
  input  clk,
  output [11:0] rd
);

  D_Flip_Flop d_ff_1 (.D(ld[11]), .clk(clk), .Q(rd[11]), .en(en));
  D_Flip_Flop d_ff_2 (.D(ld[10]), .clk(clk), .Q(rd[10]), .en(en));
  D_Flip_Flop d_ff_3 (.D(ld[9]), .clk(clk), .Q(rd[9]), .en(en));
  D_Flip_Flop d_ff_4 (.D(ld[8]), .clk(clk), .Q(rd[8]), .en(en));
  D_Flip_Flop d_ff_5 (.D(ld[6]), .clk(clk), .Q(rd[6]), .en(en));
  D_Flip_Flop d_ff_6 (.D(ld[7]), .clk(clk), .Q(rd[7]), .en(en));
  D_Flip_Flop d_ff_7 (.D(ld[5]), .clk(clk), .Q(rd[5]), .en(en));
  D_Flip_Flop d_ff_8 (.D(ld[4]), .clk(clk), .Q(rd[4]), .en(en));
  D_Flip_Flop d_ff_9 (.D(ld[3]), .clk(clk), .Q(rd[3]), .en(en));
  D_Flip_Flop d_ff_10 (.D(ld[2]), .clk(clk), .Q(rd[2]), .en(en));
  D_Flip_Flop d_ff_11 (.D(ld[1]), .clk(clk), .Q(rd[1]), .en(en));
  D_Flip_Flop d_ff_12 (.D(ld[0]), .clk(clk), .Q(rd[0]), .en(en));
endmodule

module Register_16 (
  input  [15:0] ld,
  input  en,
  input  clk,
  output [15:0] rd
);

  D_Flip_Flop d_ff_1 (.D(ld[14]), .clk(clk), .Q(rd[14]), .en(en));
  D_Flip_Flop d_ff_2 (.D(ld[15]), .clk(clk), .Q(rd[15]), .en(en));
  D_Flip_Flop d_ff_3 (.D(ld[13]), .clk(clk), .Q(rd[13]), .en(en));
  D_Flip_Flop d_ff_4 (.D(ld[12]), .clk(clk), .Q(rd[12]), .en(en));
  D_Flip_Flop d_ff_5 (.D(ld[10]), .clk(clk), .Q(rd[10]), .en(en));
  D_Flip_Flop d_ff_6 (.D(ld[11]), .clk(clk), .Q(rd[11]), .en(en));
  D_Flip_Flop d_ff_7 (.D(ld[9]), .clk(clk), .Q(rd[9]), .en(en));
  D_Flip_Flop d_ff_8 (.D(ld[8]), .clk(clk), .Q(rd[8]), .en(en));
  D_Flip_Flop d_ff_9 (.D(ld[7]), .clk(clk), .Q(rd[7]), .en(en));
  D_Flip_Flop d_ff_10 (.D(ld[6]), .clk(clk), .Q(rd[6]), .en(en));
  D_Flip_Flop d_ff_11 (.D(ld[5]), .clk(clk), .Q(rd[5]), .en(en));
  D_Flip_Flop d_ff_12 (.D(ld[4]), .clk(clk), .Q(rd[4]), .en(en));
  D_Flip_Flop d_ff_13 (.D(ld[3]), .clk(clk), .Q(rd[3]), .en(en));
  D_Flip_Flop d_ff_14 (.D(ld[2]), .clk(clk), .Q(rd[2]), .en(en));
  D_Flip_Flop d_ff_15 (.D(ld[1]), .clk(clk), .Q(rd[1]), .en(en));
  D_Flip_Flop d_ff_16 (.D(ld[0]), .clk(clk), .Q(rd[0]), .en(en));
endmodule

module D_Flip_Flop (
  input  D,
  input  clk,
  input  en,
  output Q
);

  wire not_1_out;

  not not_1 (not_1_out, D);
  S_R_Flip_Flop s_r_ff_1 (.S(D), .clk(clk), .R(not_1_out), .Q(Q), .en(en));  // open: Qn, preset, reset
endmodule

module Instruction_Decoder (
  input  [11:0] instr,
  output [2:0] dr,
  output [2:0] sr1,
  output [2:0] sr2,
  output [3:0] ALUC,
  output [11:0] jmp
);

  wire and_1_out;
  wire [3:0] bit_extender_1_out;

  and and_1 (and_1_out, instr[10], instr[11]);
  assign bit_extender_1_out = {{1{1'b0}}, instr[11:9]};  // Bit_Extender bit_extender_1
  Multiplexer #(.width(4), .enable("false")) multiplexer_1 (
    .in0(bit_extender_1_out), .in1(instr[9:6]), .out(ALUC), .sel(and_1_out));

  assign dr = instr[2:0];
  assign jmp = instr;
  assign sr1 = instr[5:3];
  assign sr2 = instr[8:6];
endmodule

module IR (
  input  [11:0] ld,
  input  en,
  input  clk,
  output [11:0] rd
);

  Register_12 register_12_1 (.ld(ld), .en(en), .clk(clk), .rd(rd));
endmodule

module ZF (
  input  ld,
  input  en,
  input  clk,
  output rd
);

  D_Flip_Flop d_ff_1 (.D(ld), .clk(clk), .Q(rd), .en(en));
endmodule

module Data_Receiver (
  input  [15:0] din,
  output [11:0] instr,
  output [2:0] opc
);


  assign instr = din[11:0];
  assign opc = din[14:12];
endmodule

module Data_Transmitter (
  input  [11:0] pc,
  input  [15:0] R1,
  input  s,
  output [11:0] addr
);

  Multiplexer #(.width(12), .enable("false")) multiplexer_1 (.in0(pc), .in1(R1[11:0]), .out(addr), .sel(s));
endmodule

module State_Manager (
  input  [2:0] opc,
  input  z,
  input  clk,
  output [2:0] state
);

  wire [2:0] Next_State_next;

  Next_State Next_State (.opc(opc), .state(state), .z(z), .next(Next_State_next));
  Register_3 u_state (.ld(Next_State_next), .en(1'b1), .clk(clk), .rd(state));
endmodule

module Next_State (
  input  [2:0] opc,
  input  [2:0] state,
  input  z,
  output [2:0] next
);

  wire and_1_out, and_2_out, and_3_out, and_4_out, and_5_out, and_6_out, and_7_out, and_8_out, not_1_out,
       not_2_out, not_3_out, not_4_out, not_5_out, not_6_out, not_7_out, not_8_out, not_9_out, not_10_out,
       not_11_out, not_12_out, not_13_out, not_14_out, not_15_out, not_16_out, not_17_out, not_18_out,
       not_19_out, not_20_out, not_21_out, not_22_out, not_23_out, not_24_out, not_25_out, not_26_out,
       not_27_out, not_28_out, not_29_out, not_30_out, not_31_out, not_32_out, not_33_out;

  not not_1 (not_1_out, opc[1]);
  not not_2 (not_2_out, opc[0]);
  not not_3 (not_3_out, state[2]);
  not not_4 (not_4_out, state[1]);
  not not_5 (not_5_out, state[0]);
  not not_6 (not_6_out, opc[1]);
  not not_7 (not_7_out, state[2]);
  not not_8 (not_8_out, state[1]);
  not not_9 (not_9_out, state[0]);
  not not_10 (not_10_out, state[2]);
  not not_11 (not_11_out, state[1]);
  not not_12 (not_12_out, state[0]);
  not not_13 (not_13_out, opc[2]);
  not not_14 (not_14_out, opc[0]);
  not not_15 (not_15_out, state[2]);
  not not_16 (not_16_out, state[1]);
  not not_17 (not_17_out, state[0]);
  not not_18 (not_18_out, opc[2]);
  not not_19 (not_19_out, state[2]);
  not not_20 (not_20_out, state[1]);
  not not_21 (not_21_out, state[0]);
  not not_22 (not_22_out, opc[2]);
  not not_23 (not_23_out, opc[1]);
  not not_24 (not_24_out, state[2]);
  not not_25 (not_25_out, state[1]);
  not not_26 (not_26_out, state[0]);
  not not_27 (not_27_out, opc[2]);
  not not_28 (not_28_out, state[2]);
  not not_29 (not_29_out, state[1]);
  not not_30 (not_30_out, state[0]);
  not not_31 (not_31_out, state[2]);
  not not_32 (not_32_out, state[1]);
  not not_33 (not_33_out, state[0]);
  and and_1 (and_1_out, opc[2], not_1_out, not_2_out, not_3_out, not_4_out, not_5_out, z);
  and and_2 (and_2_out, opc[2], not_6_out, opc[0], not_7_out, not_8_out, not_9_out);
  and and_3 (and_3_out, opc[2], opc[1], opc[0], not_10_out, not_11_out, not_12_out);
  and and_4 (and_4_out, not_13_out, opc[1], not_14_out, not_15_out, not_16_out, not_17_out);
  and and_5 (and_5_out, not_18_out, opc[1], opc[0], not_19_out, not_20_out, not_21_out);
  and and_6 (and_6_out, not_22_out, not_23_out, opc[0], not_24_out, not_25_out, not_26_out);
  and and_7 (and_7_out, not_27_out, opc[1], opc[0], not_28_out, not_29_out, not_30_out);
  and and_8 (and_8_out, opc[2], opc[1], opc[0], not_31_out, not_32_out, not_33_out);
  or or_1 (next[2], and_1_out, and_2_out, and_3_out);
  or or_2 (next[1], and_4_out, and_5_out);
  or or_3 (next[0], and_6_out, and_7_out, and_8_out);

  // Notes on the sheet:
  //   This circuit belongs to the hardwired control unit
endmodule

module Register_3 (
  input  [2:0] ld,
  input  en,
  input  clk,
  output [2:0] rd
);

  D_Flip_Flop d_ff_1 (.D(ld[2]), .clk(clk), .Q(rd[2]), .en(en));
  D_Flip_Flop d_ff_2 (.D(ld[0]), .clk(clk), .Q(rd[0]), .en(en));
  D_Flip_Flop d_ff_3 (.D(ld[1]), .clk(clk), .Q(rd[1]), .en(en));
endmodule

module Signal_Generator (
  input  [2:0] state,
  output PCINC,
  output IRLD,
  output ARMUX,
  output MUX,
  output PCLD,
  output REGLD,
  output ZFLD,
  output MEMLD
);

  wire and_1_out, and_2_out, and_4_out, and_5_out, and_6_out, and_7_out, and_9_out, and_10_out, and_11_out,
       not_1_out, not_2_out, not_3_out, not_4_out, not_5_out, not_6_out, not_7_out, not_8_out, not_9_out,
       not_10_out, not_11_out, not_12_out, not_13_out, not_14_out, not_15_out, not_16_out, not_17_out,
       not_18_out, not_19_out, not_20_out, not_21_out, not_22_out, not_23_out, not_24_out;

  not not_1 (not_1_out, state[2]);
  not not_2 (not_2_out, state[1]);
  not not_3 (not_3_out, state[0]);
  not not_4 (not_4_out, state[2]);
  not not_5 (not_5_out, state[1]);
  not not_6 (not_6_out, state[2]);
  not not_7 (not_7_out, state[1]);
  not not_8 (not_8_out, state[0]);
  not not_9 (not_9_out, state[2]);
  not not_10 (not_10_out, state[0]);
  not not_11 (not_11_out, state[2]);
  not not_12 (not_12_out, state[2]);
  not not_13 (not_13_out, state[1]);
  not not_14 (not_14_out, state[2]);
  not not_15 (not_15_out, state[0]);
  not not_16 (not_16_out, state[1]);
  not not_17 (not_17_out, state[0]);
  not not_18 (not_18_out, state[2]);
  not not_19 (not_19_out, state[1]);
  not not_20 (not_20_out, state[2]);
  not not_21 (not_21_out, state[0]);
  not not_22 (not_22_out, state[1]);
  not not_23 (not_23_out, state[1]);
  not not_24 (not_24_out, state[2]);
  and and_1 (and_1_out, not_1_out, not_2_out, not_3_out);
  and and_2 (and_2_out, not_4_out, not_5_out, state[0]);
  and and_3 (IRLD, not_6_out, not_7_out, not_8_out);
  and and_4 (and_4_out, not_9_out, state[1], not_10_out);
  and and_5 (and_5_out, not_11_out, state[1], state[0]);
  and and_6 (and_6_out, not_12_out, not_13_out, state[0]);
  and and_7 (and_7_out, not_14_out, state[1], not_15_out);
  and and_8 (PCLD, state[2], not_16_out, not_17_out);
  and and_9 (and_9_out, not_18_out, not_19_out, state[0]);
  and and_10 (and_10_out, not_20_out, state[1], not_21_out);
  and and_11 (and_11_out, state[2], not_22_out, state[0]);
  and and_12 (ZFLD, state[2], not_23_out, state[0]);
  and and_13 (MEMLD, not_24_out, state[1], state[0]);
  or or_1 (PCINC, and_1_out, and_2_out);
  or or_2 (ARMUX, and_4_out, and_5_out);
  or or_3 (MUX, and_6_out, and_7_out);
  or or_4 (REGLD, and_9_out, and_10_out, and_11_out);

  // Notes on the sheet:
  //   This circuit belongs to the hardwired control unit
endmodule

module Simulation (
);

  wire clk_out, cpu_1_memld;
  wire [2:0] n7_segment_hex_adapter_1_edc, n7_segment_hex_adapter_2_edc, n7_segment_hex_adapter_3_edc,
       n7_segment_hex_adapter_4_edc;
  wire [3:0] n7_segment_hex_adapter_1_gfab, n7_segment_hex_adapter_2_gfab, n7_segment_hex_adapter_3_gfab,
       n7_segment_hex_adapter_4_gfab;
  wire [11:0] cpu_1_addrout;
  wire [15:0] cpu_1_dout, cpu_1_r0, ram_1_data;

  Clock clk (.out(clk_out));
  CPU cpu_1 (
    .din(ram_1_data), .clk(clk_out), .MEMLD(cpu_1_memld), .Addrout(cpu_1_addrout), .Dout(cpu_1_dout),
    .R0(cpu_1_r0));
  _7_Segment_Hex_Adapter u_7_segment_hex_adapter_1 (
    .num(cpu_1_r0[15:12]), .edc(n7_segment_hex_adapter_1_edc), .gfab(n7_segment_hex_adapter_1_gfab));
  _7_Segment_Display u_7_segment_display_1 (
    .g(n7_segment_hex_adapter_1_gfab[3]), .f(n7_segment_hex_adapter_1_gfab[2]),
    .a(n7_segment_hex_adapter_1_gfab[1]), .b(n7_segment_hex_adapter_1_gfab[0]),
    .e(n7_segment_hex_adapter_1_edc[2]), .d(n7_segment_hex_adapter_1_edc[1]),
    .c(n7_segment_hex_adapter_1_edc[0]));  // open: dp
  RAM #(.addrWidth(12), .dataWidth(16), .bus("separate")) ram_1 (
    .addr(cpu_1_addrout), .din(cpu_1_dout), .data(ram_1_data), .str(cpu_1_memld), .clk(clk_out), .ld(1'b1));  // open: sel, clr
  _7_Segment_Hex_Adapter u_7_segment_hex_adapter_2 (
    .num(cpu_1_r0[11:8]), .edc(n7_segment_hex_adapter_2_edc), .gfab(n7_segment_hex_adapter_2_gfab));
  _7_Segment_Hex_Adapter u_7_segment_hex_adapter_3 (
    .num(cpu_1_r0[7:4]), .edc(n7_segment_hex_adapter_3_edc), .gfab(n7_segment_hex_adapter_3_gfab));
  _7_Segment_Display u_7_segment_display_2 (
    .g(n7_segment_hex_adapter_3_gfab[3]), .f(n7_segment_hex_adapter_3_gfab[2]),
    .a(n7_segment_hex_adapter_3_gfab[1]), .b(n7_segment_hex_adapter_3_gfab[0]),
    .e(n7_segment_hex_adapter_3_edc[2]), .d(n7_segment_hex_adapter_3_edc[1]),
    .c(n7_segment_hex_adapter_3_edc[0]));  // open: dp
  _7_Segment_Display u_7_segment_display_3 (
    .g(n7_segment_hex_adapter_2_gfab[3]), .f(n7_segment_hex_adapter_2_gfab[2]),
    .a(n7_segment_hex_adapter_2_gfab[1]), .b(n7_segment_hex_adapter_2_gfab[0]),
    .e(n7_segment_hex_adapter_2_edc[2]), .d(n7_segment_hex_adapter_2_edc[1]),
    .c(n7_segment_hex_adapter_2_edc[0]));  // open: dp
  _7_Segment_Hex_Adapter u_7_segment_hex_adapter_4 (
    .num(cpu_1_r0[3:0]), .edc(n7_segment_hex_adapter_4_edc), .gfab(n7_segment_hex_adapter_4_gfab));
  _7_Segment_Display u_7_segment_display_4 (
    .g(n7_segment_hex_adapter_4_gfab[3]), .f(n7_segment_hex_adapter_4_gfab[2]),
    .a(n7_segment_hex_adapter_4_gfab[1]), .b(n7_segment_hex_adapter_4_gfab[0]),
    .e(n7_segment_hex_adapter_4_edc[2]), .d(n7_segment_hex_adapter_4_edc[1]),
    .c(n7_segment_hex_adapter_4_edc[0]));  // open: dp
endmodule

module _7_Segment_Hex_Adapter (
  input  [3:0] num,
  output [2:0] edc,
  output [3:0] gfab
);

  wire and_1_out, and_2_out, and_3_out, and_4_out, and_5_out, and_6_out, and_7_out, and_8_out, and_9_out,
       and_10_out, and_11_out, and_12_out, and_13_out, and_14_out, and_15_out, and_16_out, and_17_out,
       and_18_out, and_19_out, and_20_out, and_21_out, and_22_out, and_23_out, and_24_out, and_25_out,
       and_26_out, and_27_out, and_28_out, and_29_out, and_30_out, and_31_out, and_32_out, and_33_out,
       and_34_out, and_35_out, not_1_out, not_2_out, not_3_out, not_4_out, not_5_out, not_6_out, not_7_out,
       not_8_out, not_9_out, not_10_out, not_11_out, not_12_out, not_13_out, not_14_out, not_15_out,
       not_16_out, not_17_out, not_18_out, not_19_out, not_20_out, not_21_out, not_22_out, not_23_out,
       not_24_out, not_25_out, not_26_out, not_27_out, not_28_out, not_29_out, not_30_out, not_31_out,
       not_32_out, not_33_out, not_34_out, not_35_out, not_36_out, not_37_out, not_38_out, not_39_out,
       not_40_out, not_41_out, not_42_out, not_43_out;

  not not_1 (not_1_out, num[2]);
  and and_1 (and_1_out, not_1_out, not_2_out);
  not not_2 (not_2_out, num[0]);
  not not_3 (not_3_out, num[3]);
  and and_2 (and_2_out, not_3_out, num[1]);
  not not_4 (not_4_out, num[3]);
  and and_3 (and_3_out, not_4_out, num[2], num[0]);
  and and_4 (and_4_out, num[2], num[1]);
  and and_5 (and_5_out, num[3], not_5_out, not_6_out);
  not not_5 (not_5_out, num[2]);
  not not_6 (not_6_out, num[1]);
  and and_6 (and_6_out, num[3], not_7_out);
  not not_7 (not_7_out, num[0]);
  not not_8 (not_8_out, num[3]);
  and and_7 (and_7_out, not_8_out, not_9_out);
  not not_9 (not_9_out, num[2]);
  not not_10 (not_10_out, num[3]);
  and and_8 (and_8_out, not_10_out, not_11_out, not_12_out);
  not not_11 (not_11_out, num[1]);
  not not_12 (not_12_out, num[0]);
  not not_13 (not_13_out, num[2]);
  and and_9 (and_9_out, not_13_out, not_14_out);
  not not_14 (not_14_out, num[0]);
  not not_15 (not_15_out, num[3]);
  and and_10 (and_10_out, not_15_out, num[1], num[0]);
  not not_16 (not_16_out, num[1]);
  and and_11 (and_11_out, num[3], not_16_out, num[0]);
  not not_17 (not_17_out, num[3]);
  and and_12 (and_12_out, not_17_out, not_18_out);
  not not_18 (not_18_out, num[1]);
  not not_19 (not_19_out, num[3]);
  and and_13 (and_13_out, not_19_out, num[0]);
  not not_20 (not_20_out, num[1]);
  and and_14 (and_14_out, not_20_out, num[0]);
  not not_21 (not_21_out, num[3]);
  and and_15 (and_15_out, not_21_out, num[2]);
  and and_16 (and_16_out, num[3], not_22_out);
  not not_22 (not_22_out, num[2]);
  not not_23 (not_23_out, num[3]);
  not not_24 (not_24_out, num[2]);
  and and_17 (and_17_out, not_23_out, not_24_out, not_25_out);
  not not_25 (not_25_out, num[0]);
  not not_26 (not_26_out, num[2]);
  and and_18 (and_18_out, not_26_out, num[1], num[0]);
  and and_19 (and_19_out, num[2], not_27_out, num[0]);
  not not_27 (not_27_out, num[1]);
  and and_20 (and_20_out, num[2], num[1], not_28_out);
  not not_28 (not_28_out, num[0]);
  and and_21 (and_21_out, num[3], not_29_out);
  not not_29 (not_29_out, num[1]);
  not not_30 (not_30_out, num[2]);
  and and_22 (and_22_out, not_30_out, not_31_out);
  not not_31 (not_31_out, num[0]);
  and and_23 (and_23_out, num[1], not_32_out);
  not not_32 (not_32_out, num[0]);
  and and_24 (and_24_out, num[3], num[1]);
  and and_25 (and_25_out, num[3], num[2]);
  not not_33 (not_33_out, num[1]);
  and and_26 (and_26_out, not_33_out, not_34_out);
  not not_34 (not_34_out, num[0]);
  not not_35 (not_35_out, num[3]);
  and and_27 (and_27_out, not_35_out, num[2], not_36_out);
  not not_36 (not_36_out, num[1]);
  and and_28 (and_28_out, num[2], not_37_out);
  not not_37 (not_37_out, num[0]);
  and and_29 (and_29_out, num[3], not_38_out);
  not not_38 (not_38_out, num[2]);
  and and_30 (and_30_out, num[3], num[1]);
  not not_39 (not_39_out, num[2]);
  and and_31 (and_31_out, not_39_out, num[1]);
  and and_32 (and_32_out, num[1], not_40_out);
  not not_40 (not_40_out, num[0]);
  not not_41 (not_41_out, num[3]);
  and and_33 (and_33_out, not_41_out, num[2], not_42_out);
  not not_42 (not_42_out, num[1]);
  and and_34 (and_34_out, num[3], not_43_out);
  not not_43 (not_43_out, num[2]);
  and and_35 (and_35_out, num[3], num[0]);
  or or_1 (gfab[0], and_7_out, and_8_out, and_9_out, and_10_out, and_11_out);
  or or_2 (edc[0], and_12_out, and_13_out, and_14_out, and_15_out, and_16_out);
  or or_3 (edc[1], and_17_out, and_18_out, and_19_out, and_20_out, and_21_out);
  or or_4 (edc[2], and_22_out, and_23_out, and_24_out, and_25_out);
  or or_5 (gfab[2], and_26_out, and_27_out, and_28_out, and_29_out, and_30_out);
  or or_6 (gfab[3], and_31_out, and_32_out, and_33_out, and_34_out, and_35_out);
  or or_7 (gfab[1], and_1_out, and_2_out, and_3_out, and_4_out, and_5_out, and_6_out);
endmodule

module Control_Unit_Microprogrammed (
  input  z,
  input  [2:0] opc,
  input  clk,
  output PCINC,
  output MUX,
  output ARMUX,
  output IRLD,
  output PCLD,
  output REGLD,
  output ZFLD,
  output MEMLD
);

  wire and_1_out, or_1_out;
  wire [2:0] multiplexer_1_out, register_3_1_rd;

  or or_1 (or_1_out, ~IRLD, and_1_out);  // OR_Gate
  and and_1 (and_1_out, opc[2], ~opc[0], ~z);  // AND_Gate
  Register_3 register_3_1 (.ld(multiplexer_1_out), .en(1'b1), .clk(clk), .rd(register_3_1_rd));
  Multiplexer #(.width(3), .enable("false")) multiplexer_1 (
    .in0(opc), .in1(3'b000), .out(multiplexer_1_out), .sel(or_1_out));
  ROM #(.addrWidth(3)) rom_1 (
    .addr(register_3_1_rd), .data({PCINC, MUX, ARMUX, IRLD, PCLD, REGLD, ZFLD, MEMLD}), .sel(1'b1));

  // Notes on the sheet:
  //   contents of rom_1 (hex, n*v repeats v):
  //   90 c4 64 21 8 8 0 6
endmodule
